# Fritzing sketch Untitled Sketch 2 (saved by Fritzing 1.0.1rc)

parts:
  Button_A = Pushbutton [package="[SMD]"]
  Button_B = Pushbutton [package="[SMD]"]
  Button_X = Pushbutton [package="[SMD]"]
  Grove1 = Grove OLED 128x96
  Mod1 = Raspberry Pi Pico

nets (from the breadboard view):
  N1: Button_A.Pin_1, Button_A.Pin_2, Button_B.Pin_1, Button_B.Pin_2, Button_X.Pin_1, Button_X.Pin_2, Grove1.GND, Mod1.pin_18, Mod1.pin_28
  N2: Button_A.Pin_3, Button_A.Pin_4, Mod1.pin_4
  N3: Button_B.Pin_3, Button_B.Pin_4, Mod1.pin_5
  N4: Button_X.Pin_3, Button_X.Pin_4, Mod1.pin_6
  N5: Grove1.VCC, Mod1.pin_36
  N6: Grove1.SDA, Mod1.pin_1
  N7: Grove1.SCL, Mod1.pin_2

custom parts:
  Raspberry Pi Pico: Raspberry Pi Pico. Based around the RP2040 microcontroller the Pico is a low cost microcontroller device bringing Raspberry Pi quality, cost, and easy of use to the microcontroller space. Jan 2021, Split part in to two versions: tht (this one) and SMD. This one will drill holes for a .1 in header in pcb to allow plugging in the module as well as providing pads to solder the module to the top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
